// Logisim project cpu.circ as structural Verilog: 1 circuit, main circuit cpu
module cpu (
  input  in_1,
  input  in_2,
  input  in_3
);

  wire EXCLK, IDCLK, IFCLK, isJAL, isRes, isWriteRD, MEMCLK, not_1_out, syscall, WBCLK, WriteReg, zero;
  wire [1:0] PCcontrol;
  wire [3:0] Byte;
  wire [4:0] multiplexer_2_out, multiplexer_3_out;
  wire [25:0] ADD;
  wire [31:0] adder_1_out, DataMem_p5, imm32, multiplexer_4_out, nPC, PC, PC4, res, rsdata, rtdata,
       shifter_1_out, writedata;
  wire [31:26] INS;

  Shifter #(.width(32)) shifter_1 (.in(imm32), .\dist (5'b00010), .out(shifter_1_out));
  Register #(.width(32)) u_PC (.D(nPC), .en(not_1_out), .clk(WBCLK), .Q(PC));  // open: clr
  not not_1 (not_1_out, syscall);
  Adder #(.width(32)) adder_1 (.a(PC4), .b(shifter_1_out), .out(adder_1_out));  // open: cin, cout
  Adder #(.width(32)) adder_2 (.a(PC), .b(32'h4), .out(PC4));  // open: cin, cout
  assign imm32 = {{16{ADD[15]}}, ADD[15:0]};  // Bit_Extender bit_extender_1
  Multiplexer #(.select(2), .width(32)) multiplexer_1 (
    .in0(PC4), .in1(adder_1_out), .in2(res), .in3({PC[31:28], ADD, 2'b00}), .out(nPC), .sel(PCcontrol));
  // mem InstMem: pin names not known; wires that end beside it: PC, 4'b0000, {32{1'b0}}, IFCLK, {INS, ADD}
  fiveCounter fivecounter_1 (
    .Start(in_1), .Clk(in_2), .miss(in_3), .S_IF(IFCLK), .S_ID(IDCLK), .S_EX(EXCLK), .S_MEM(MEMCLK),
    .S_WB(WBCLK));
  Multiplexer #(.width(5)) multiplexer_2 (.in0(ADD[20:16]), .in1(ADD[15:11]), .out(multiplexer_2_out), .sel(isWriteRD));
  Multiplexer #(.width(5)) multiplexer_3 (
    .in0(multiplexer_2_out), .in1({5{1'b1}}), .out(multiplexer_3_out), .sel(isJAL));
  Multiplexer #(.width(32)) multiplexer_4 (.in0(writedata), .in1(PC4), .out(multiplexer_4_out), .sel(isJAL));
  // ALU_Control alu_control_1: pin names not known; wires that end beside it: rsdata, rtdata, ADD[10:6], INS, ADD[5:0], isRes, isJAL, isWriteRD, syscall, Byte, WriteReg
  // regfile RegisterFile: pin names not known; wires that end beside it: ADD[25:21], ADD[20:16], multiplexer_3_out, multiplexer_4_out, WriteReg, IDCLK, rsdata, rtdata
  ALU alu_1 (
    .rs(rsdata), .rt(rtdata), .imm(imm32), .shiftAmount(ADD[10:6]), .opcode(INS), .func(ADD[5:0]),
    .result(res), .zero(zero), .PCcontrol(PCcontrol));
  // mem DataMem: pin names not known; wires that end beside it: res, Byte, rtdata, MEMCLK, DataMem_p5
  Multiplexer #(.width(32)) multiplexer_5 (.in0(DataMem_p5), .in1(res), .out(writedata), .sel(isRes));

  // Other names for the same wires on the sheet: func[5:0] = ADD[5:0]; imm[15:0] = ADD[15:0]; INS[25:0] = ADD;
  //   sa[4:0] = ADD[10:6]; rd[4:0] = ADD[15:11]; rt[4:0] = ADD[20:16]; rs[4:0] = ADD[25:21]; OP[5:0] = INS

  // Notes on the sheet:
  //   PC Control
endmodule
